// Logisim project HW3.circ as structural Verilog: 1 circuit, main circuit main
// D1
module main (
);

  wire and_1_out, and_2_out, clock_1_out, clock_2_out, d_ff_1_q, d_ff_2_q, d_ff_3_q, not_1_out, not_2_out,
       not_3_out, or_1_out, or_2_out, xor_1_out;
  wire [7:0] ram_1_data, register_1_q, register_2_q;

  Clock clock_1 (.out(clock_1_out));
  Clock clock_2 (.out(clock_2_out));
  Register register_1 (.Q(register_1_q), .clk(clock_1_out));  // open: D, en, clr
  Register register_2 (.Q(register_2_q), .clk(clock_1_out));  // open: D, en, clr
  D_Flip_Flop d_ff_1 (.clk(clock_2_out), .D(not_1_out), .Q(d_ff_1_q));  // open: Qn, preset, en, reset
  D_Flip_Flop d_ff_2 (.clk(clock_2_out), .D(xor_1_out), .Q(d_ff_2_q));  // open: Qn, preset, en, reset
  D_Flip_Flop d_ff_3 (.clk(clock_2_out), .D(or_2_out), .Q(d_ff_3_q));  // open: Qn, preset, en, reset
  not not_1 (not_1_out, d_ff_1_q);
  not not_2 (not_2_out, d_ff_2_q);
  not not_3 (not_3_out, d_ff_3_q);
  RAM #(.bus("separate")) ram_1 (
    .addr(register_1_q), .din(register_2_q), .data(ram_1_data), .clk(clock_1_out));  // open: str, sel, ld, clr
  xor xor_1 (xor_1_out, d_ff_1_q, d_ff_2_q);
  or or_1 (or_1_out, not_1_out, not_2_out);
  Register register_3 (.D(ram_1_data), .clk(clock_1_out));  // open: en, Q, clr
  and and_1 (and_1_out, or_1_out, d_ff_3_q);
  and and_2 (and_2_out, not_3_out, d_ff_2_q, d_ff_1_q);
  LED led_1 (.in(d_ff_1_q));
  LED led_2 (.in(d_ff_2_q));
  LED led_3 (.in(d_ff_3_q));
  or or_2 (or_2_out, and_1_out, and_2_out);

  // Notes on the sheet:
  //   1)
  //   2)
  //   NOT (Q1)
  //   XOR (Q1, Q2)
  //   Q3.(Q1’ + Q2’) + (Q3’.Q2.Q1)
endmodule
