// Logisim project hw2.circ as structural Verilog: 1 circuit, main circuit main
// bl
module main (
  input  [2:0] in_1,
  input  [2:0] in_2,
  input  [7:0] in_3,
  input  [7:0] in_4,
  input  [2:0] in_5
);

  wire clock_1_out, clock_2_out, decoder_1_out1, decoder_1_out2, decoder_1_out3, decoder_1_out4,
       decoder_1_out5, decoder_1_out6, decoder_1_out7, decoder_2_out1, decoder_2_out2, decoder_2_out3,
       decoder_2_out4, decoder_2_out5, decoder_2_out6, decoder_2_out7, or_1_out, or_2_out;
  wire [1:0] or_3_out;
  wire [2:0] register_1_q;
  wire [7:0] adder_1_out, shifter_1_out;

  Decoder #(.select(3), .enable("false")) decoder_1 (
    .out1(decoder_1_out1), .out2(decoder_1_out2), .out3(decoder_1_out3), .out4(decoder_1_out4),
    .out5(decoder_1_out5), .out6(decoder_1_out6), .out7(decoder_1_out7), .sel(register_1_q));  // open: out0
  Register #(.width(3)) register_1 (.D(in_2), .Q(register_1_q), .clk(clock_1_out));  // open: en, clr
  Clock clock_1 (.out(clock_1_out));
  Decoder #(.select(3), .enable("false")) decoder_2 (
    .out1(decoder_2_out1), .out2(decoder_2_out2), .out3(decoder_2_out3), .out4(decoder_2_out4),
    .out5(decoder_2_out5), .out6(decoder_2_out6), .out7(decoder_2_out7), .sel(in_1));  // open: out0
  or or_1 (or_1_out, decoder_2_out1, decoder_2_out2, decoder_2_out4, decoder_2_out7);
  or or_2 (or_2_out, decoder_2_out3, decoder_2_out5, decoder_2_out6, decoder_2_out7);
  or or_3 (or_3_out[0], decoder_1_out1, decoder_1_out2, decoder_1_out4, decoder_1_out7);
  or or_4 (or_3_out[1], decoder_1_out3, decoder_1_out5, decoder_1_out6, decoder_1_out7);
  Adder adder_1 (.a(in_3), .b(in_4), .out(adder_1_out));  // open: cin, cout
  LED led_1 (.in(or_1_out));
  LED led_2 (.in(or_2_out));
  Shifter shifter_1 (.in(adder_1_out), .\dist (in_5), .out(shifter_1_out));
  Clock clock_2 (.out(clock_2_out));
  Register #(.width(2)) register_2 (.D(or_3_out), .clk(clock_1_out));  // open: en, Q, clr
  Register register_3 (.D(shifter_1_out), .clk(clock_2_out));  // open: en, Q, clr

  // Notes on the sheet:
  //   1) 
  //   2)
endmodule
